# Fritzing sketch Arduino APRS tracker v2 (saved by Fritzing 0.9.3b)
circuit board: 8.53938cm x 3.85926cm
breadboards: 1

parts:
  R1 = TRIMPOT [package=trim_pot_pth]
  C1 = Capacitor [package=axial-5mm]
  C2 = Capacitor [package=axial-5mm]
  R4 = Resistor [tolerance=±5% resistance=1k package=THT]
  R2 = Resistor [tolerance=±5% resistance=10k package=THT]
  R3 = Resistor [tolerance=±5% resistance=10k package=THT]
  pwr+ = female pin header, 2 pins [form="♀ (female)"]
  GPS = mystery part, 4 pins [chip_label=GPS]
  Q1 = NPN-Transistor [package="TO92 [THT]"]
  TRRS = mystery part, 4 pins [chip_label=?]
  Proc = Arduino Pro Mini (5V)
  TNC = Arduino Pro Mini (5V)

nets:
  N1: R1.CCW, TNC.D6
  N2: R1.WIPER, C1.2
  GND: R1.CW, R2.Pin_1, pwr+.pin2, GPS.pin4, Q1.C, TRRS.pin1, Proc.GND, TNC.GND
  N3: C1.1, TRRS.pin2
  N4: C2.1, R2.Pin_0, R3.Pin_0
  N5: C2.2, TRRS.pin4
  N6: R4.Pin_0, Q1.B
  N7: R4.Pin_1, TNC.D10
  N8: R3.Pin_1, TNC.VCC
  N9: pwr+.pin1, Proc.RAW, TNC.RAW
  N10: GPS.pin1, Proc.VCC
  N11: GPS.pin2, Proc.MOSI
  N12: GPS.pin3, Proc.D10
  N13: Q1.E, TRRS.pin3
  N14: Proc.RXI, TNC.TXO
  N15: Proc.TXO, TNC.RXI

custom parts:
  Arduino Pro Mini (5V): It's blue! It's thin! It's the Arduino Pro Mini! SparkFun's minimal design approach to Arduino. This is a 5V Arduino running the 16MHz bootloader. Arduino Pro Mini does not come with connectors populated so that you can solder in any connector or wire with any orientation you need. We recommend first time Arduino users start with the Uno R3. It's a great board that will get you up and running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
