# Fritzing sketch Arduino APRS tracker (saved by Fritzing 0.9.3b)
circuit board: 5.89081cm x 6.62408cm
breadboards: 1

parts:
  J1 = male pin header, 2 pins [form="♂ (male)"]
  J2 = male pin header, 4 pins [form="♂ (male)"]
  TNC = Arduino Pro Mini (5V)
  TR1 = NPN-Transistor [package="TO92 [THT]"]
  J4 = Generic male header - 4 pins [form="♂ (male)" package=THT]
  R1 = Resistor [tolerance=±5% resistance=1k package=THT]
  C1 = Ceramic Capacitor [capacitance=100nF package="100 mil [THT, multilayer]"]
  R2 = Trimmer Potentiometer [maximum_resistance=10kΩ package=THT]
  R3 = Resistor [tolerance=±5% resistance=10 package=THT]
  R4 = Resistor [tolerance=±5% resistance=10 package=THT]
  Host = Arduino Pro Mini (5V)
  C2 = Ceramic Capacitor [capacitance=10nF package="100 mil [THT, multilayer]"]

nets:
  N1: J1.pin1, TNC.RAW, Host.RAW
  GND: J1.pin2, J2.pin4, TNC.GND, TR1.C, J4.gnd_blue, R2.leg1, R4.Pin_0, Host.GND
  VCC: J2.pin1, TNC.VCC, R3.Pin_0, Host.VCC
  N2: J2.pin2, Host.D10
  N3: TNC.TXO, Host.D3
  N4: TNC.RXI, Host.D4
  N5: TNC.A0, R3.Pin_1, R4.Pin_1, C2.0
  N6: TNC.D10, R1.Pin_0
  N7: TNC.D6, R2.wiper
  N8: TR1.E, J4.ptt_bare
  N9: TR1.B, R1.Pin_1
  N10: J4.tx_red, C1.1
  N11: J4.rx_green, C2.1
  N12: C1.0, R2.leg2

custom parts:
  Generic male header - 4 pins: Generic male header
