# Fritzing sketch Arduino APRS tracker v3 (saved by Fritzing 0.9.3b)
circuit board: 7.80695cm x 4.51126cm
breadboards: 1

parts:
  Proc = Arduino Pro Mini (5V)
  TNC = Arduino Pro Mini (5V)
  GPS = mystery part, 4 pins [chip_label=?]
  L7808CV = Voltage Regulator [package=to-220-alt]
  Cout = Electrolytic Capacitor [capacitance=0.47mF package="200 mil [THT, electrolytic]"]
  Cin = Electrolytic Capacitor [capacitance=0.22mF package="200 mil [THT, electrolytic]"]
  13_8V = Pad [width=3 height=3 connect=center]
  GND = female pin header, 1 pin [form="♀ (female)"]
  Pad1 = Pad [width=2.1166666666666663 height=2.1200000000000001 connect=center]
  Pad2 = Pad [width=2.1166666666666663 height=2.1200000000000001 connect=center]
  Pad3 = Pad [width=2.1166666666666663 height=2.1200000000000001 connect=center]
  Pad4 = Pad [width=2.1166666666666663 height=2.1200000000000001 connect=center]
  Pad5 = Pad [width=2.1166666666666663 height=2.1200000000000001 connect=center]
  Pad6 = Pad [width=2.1166666666666663 height=2.1200000000000001 connect=center]
  Pad7 = Pad [width=2.1166666666666663 height=2.1200000000000001 connect=center]
  Pad8 = Pad [width=2.1200000000000001 height=2.1200000000000001 connect=center]
  Pad9 = Pad [width=2.1166666666666663 height=2.1200000000000001 connect=center]
  Pad10 = Pad [width=2.1166666666666663 height=2.1200000000000001 connect=center]
  Pad11 = Pad [width=2.1166666666666663 height=2.1200000000000001 connect=center]
  Pad12 = Pad [width=2.1166666666666663 height=2.1200000000000001 connect=center]
  Pad13 = Pad [width=2.1166666666666663 height=2.1200000000000001 connect=center]
  Pad14 = Pad [width=2.1166666666666663 height=2.1200000000000001 connect=center]
  Pad15 = Pad [width=2.1166666666666663 height=2.1200000000000001 connect=center]
  Pad16 = Pad [width=2.1166666666666663 height=2.1200000000000001 connect=center]
  Pad17 = Pad [width=2.1166666666666663 height=2.1200000000000001 connect=center]
  Pad18 = Pad [width=2.1166666666666663 height=2.1200000000000001 connect=center]
  Pad19 = Pad [width=2.1166666666666663 height=2.1200000000000001 connect=center]
  Pad20 = Pad [width=2.1166666666666663 height=2.1200000000000001 connect=center]

nets:
  N1: Proc.RAW, TNC.RAW, L7808CV.OUT, Cout.+
  GND: Proc.GND, TNC.GND, GPS.pin4, L7808CV.GND, Cout.-, Cin.-, GND.pin1, Pad3.pad, Pad7.pad, Pad15.pad, Pad20.pad
  N2: Proc.VCC, GPS.pin1
  N3: Proc.SCK, GPS.pin2
  N4: Proc.MISO, GPS.pin3
  N5: Proc.RXI, TNC.TXO
  N6: Proc.TXO, TNC.RXI
  N7: TNC.VCC, Pad9.pad
  N8: TNC.A0, Pad8.pad, Pad10.pad, Pad11.pad
  N9: TNC.D10, Pad17.pad
  N10: TNC.D6, Pad1.pad
  N11: L7808CV.IN, Cin.+, 13_8V.pad
  N12: Pad2.pad, Pad6.pad
  N13: Pad4.pad, Pad5.pad
  N14: Pad12.pad, Pad13.pad
  N15: Pad14.pad, Pad18.pad
  N16: Pad16.pad, Pad19.pad

notes:
  red
  tx aud
  100k pot
  10nF
  10k
  100nF
  green
  104
  rx aud
  103
  bare
  1k res
  blue
  bc548
  c
  b
  e
  https://m0lte.uk

custom parts:
  Arduino Pro Mini (5V): It's blue! It's thin! It's the Arduino Pro Mini! SparkFun's minimal design approach to Arduino. This is a 5V Arduino running the 16MHz bootloader. Arduino Pro Mini does not come with connectors populated so that you can solder in any connector or wire with any orientation you need. We recommend first time Arduino users start with the Uno R3. It's a great board that will get you up and running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
