# Fritzing sketch Arduino APRS tracker v5 (saved by Fritzing 0.9.3b)
circuit board: 9.68087cm x 8.73271cm
breadboards: 1

parts:
  TNC = Arduino Pro Mini (5V)
  Proc = Arduino Pro Mini (5V)
  Cout1 = Electrolytic Capacitor [capacitance=0.47mF package="200 mil [THT, electrolytic]"]
  Cin1 = Electrolytic Capacitor [capacitance=0.22mF package="200 mil [THT, electrolytic]"]
  L7808CV = Voltage Regulator [package=to-220-alt]
  R1 = Resistor [tolerance=±5% resistance=1k package=THT]
  R2 = Resistor [tolerance=±5% resistance=10k package=THT]
  C1_10nF = Capacitor [package=cap-pth-small2]
  BC548 = NPN-Transistor [package="TO92 [THT]"]
  R3 = TRIMPOT [package=trim_pot_pth]
  R4 = Resistor [tolerance=±5% resistance=10k package=THT]
  C2_100nF = Capacitor [package=cap-pth-small2]
  -pwr+ = Screw terminal - 2 pins [package=THT]
  DS1 = DS18B20 1-Wire Temperature Sensor [part_number=DS18B20]
  R5 = Resistor [tolerance=±5% resistance=4.7k package=THT]
  bcn_btn = Screw terminal - 2 pins [package=THT]
  R6 = Resistor [tolerance=±5% resistance=10k package=THT]
  R7 = Resistor [tolerance=±5% resistance=220 package=THT]
  R8 = Resistor [tolerance=±5% resistance=220 package=THT]
  R9 = Resistor [tolerance=±5% resistance=10k package=THT]
  R10 = Resistor [tolerance=±5% resistance=10k package=THT]
  LED_TX = LED - 3mm [color="Red (633nm)" package="3 mm [THT]"]
  LED_FIX = LED - 3mm [color="Red (633nm)" package="3 mm [THT]"]
  BC547 = NPN-Transistor [package="TO92 [THT]"]
  R11 = Resistor [tolerance=±5% resistance=1k package=THT]
  D1 = Rectifier Diode [part_number=1N4007 package="300 mil [THT]"]
  fan_sw = Screw terminal - 2 pins [package=THT]
  R12 = Resistor [tolerance=±5% resistance=10k package=THT]
  LED_spare = LED - 3mm [color="Red (633nm)" package="3 mm [THT]"]
  GPS = mystery part, 4 pins [chip_label=?]
  U2 = RELAY-2 [package=relay-g5v]
  Radio = screw terminal, 4 pins

nets:
  N1: TNC.RAW, Proc.RAW, Cout1.+, L7808CV.OUT
  GND: TNC.GND, Proc.GND, Cout1.-, Cin1.-, L7808CV.GND, BC548.C, R3.CW, R4.Pin_0, -pwr+.pin2, DS1.GND, R6.Pin_0, R8.Pin_1, R9.Pin_1, R10.Pin_1, BC547.E, R12.Pin_0, GPS.pin4, Radio.pin1
  VCC: TNC.VCC, R2.Pin_0, DS1.VDD, R5.Pin_0
  N2: TNC.A0, R2.Pin_1, C1_10nF.1, R4.Pin_1
  N3: TNC.D10, R1.Pin_1
  N4: TNC.D6, R3.CCW
  N5: TNC.RXI, Proc.D2
  N6: TNC.TXO, Proc.D3
  N7: Proc.VCC, bcn_btn.pin2, D1.cathode, GPS.pin1, U2.9
  N8: Proc.A1, R7.Pin_1, R8.Pin_0
  N9: Proc.SCK, LED_FIX.anode
  N10: Proc.MISO, GPS.pin3
  N11: Proc.MOSI, GPS.pin2
  N12: Proc.D10, LED_spare.anode
  N13: Proc.D9, LED_TX.anode
  N14: Proc.D8, bcn_btn.pin1, R6.Pin_1
  N15: Proc.D7, DS1.DQ, R5.Pin_1
  N16: Proc.D4, R11.Pin_0
  N17: Cin1.+, L7808CV.IN, -pwr+.pin1, R7.Pin_0
  N18: R1.Pin_0, BC548.B
  N19: C1_10nF.2, Radio.pin4
  N20: BC548.E, Radio.pin3
  N21: R3.WIPER, C2_100nF.2
  N22: C2_100nF.1, Radio.pin2
  N23: R9.Pin_0, LED_FIX.cathode
  N24: R10.Pin_0, LED_TX.cathode
  N25: BC547.B, R11.Pin_1
  N26: BC547.C, D1.anode, U2.2
  N27: fan_sw.pin1, U2.5
  N28: fan_sw.pin2, U2.10
  N29: R12.Pin_1, LED_spare.cathode

notes:
  VCC
  RX
  NMEAOUT
  GND
  rx ptt tx gnd
  2.5t 3.5s 3.5r 2.5s
  TX AUD
  TX audio
  RX AUD
  KISSO
  KISSI
  OWBUS
  OW
  BCN
  TXLED
  BSENS
  FIXLED
  SPLED
  NMEAIN
  TOGPS
  PTT
  https://m0lte.uk

custom parts:
  Arduino Pro Mini (5V): It's blue! It's thin! It's the Arduino Pro Mini! SparkFun's minimal design approach to Arduino. This is a 5V Arduino running the 16MHz bootloader. Arduino Pro Mini does not come with connectors populated so that you can solder in any connector or wire with any orientation you need. We recommend first time Arduino users start with the Uno R3. It's a great board that will get you up and running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
